# Fritzing sketch access_control_circuit (saved by Fritzing 0.9.3b)
breadboards: 2

parts:
  KY-008_Laserdiode1 = Laser [part_number=1219301 package=keys]
  KY-008_Laserdiode2 = Laser [part_number=1219301 package=keys]
  Q1 = NPN-Transistor [package="SOT-23 [SMD]"]
  Componente1 = Arduino Uno (Rev3)
  Q2 = NPN-Transistor [package="SOT-23 [SMD]"]
  ZS-042_RTC1 = ZS-042 RTC Module

nets:
  GND: KY-008_Laserdiode1.connector0pin, KY-008_Laserdiode2.connector0pin, Componente1.GND, Q2.2, ZS-042_RTC1.GND
  5V: KY-008_Laserdiode1.connector1pin, KY-008_Laserdiode2.connector1pin, Q1.1, Componente1.5V, Q2.1, ZS-042_RTC1.VCC
  N1: KY-008_Laserdiode1.connector2pin, Componente1.D6_PWM
  N2: KY-008_Laserdiode2.connector2pin, Componente1.D9_PWM
  N3: Q1.0, Componente1.D4
  N4: Componente1.A4/SDA, ZS-042_RTC1.SDA
  N5: Componente1.A5/SCL, ZS-042_RTC1.SCL
  N6: Componente1.D3_PWM, Q2.0

notes:
  gnd | out | vcc
  IR Phototransistors
  gnd | vcc | data
  Diode Lasers

custom parts:
  Laser: KEYES KY-008 650nm Laser Transmitter Module
